# Fritzing sketch circuit (saved by Fritzing 0.9.3b)
breadboards: 1

parts:
  S1 = Pushbutton [package="[THT]"]
  S2 = Pushbutton [package="[THT]"]
  Part1 = Arduino Mega ADK (Rev3)
  J1 = Piezo Speaker
  U1 = MLX90614 [package=to-39]
  R1 = Resistor [tolerance=±5% resistance=220 package="0805 [SMD]"]
  R2 = Resistor [tolerance=±5% resistance=220 package="0805 [SMD]"]
  LED2 = LEDs [package=led10mm]
  LED3 = LEDs [package=led10mm]
  LED4 = LEDs [package=led10mm]
  R3 = Resistor [tolerance=±5% resistance=220 package="0805 [SMD]"]
  R4 = Resistor [tolerance=±5% resistance=220 package="0805 [SMD]"]
  R5 = Resistor [tolerance=±5% resistance=220 package="0805 [SMD]"]

nets:
  N1: S1.Pin_1, S1.Pin_2, Part1.D9_PWM, R1.Pin_1
  5V: S1.Pin_3, S1.Pin_4, S2.Pin_3, S2.Pin_4, Part1.5V, U1.VDD
  N2: S2.Pin_1, S2.Pin_2, Part1.D8_PWM, R2.Pin_1
  N3: Part1.D13_PWM, R3.Pin_0
  N4: Part1.D12_PWM, R4.Pin_0
  N5: Part1.D11_PWM, R5.Pin_0
  N6: Part1.D10_PWM, J1.pin2
  GND: Part1.GND, J1.pin1, U1.VSS, R1.Pin_0, R2.Pin_0, LED2.C, LED3.C, LED4.C
  N7: Part1.D2_PWM, U1.SCL_VZ
  N8: LED2.A, R4.Pin_1
  N9: LED3.A, R5.Pin_1
  N10: LED4.A, R3.Pin_1
